# Fritzing sketch termometer (saved by Fritzing 0.9.2b)
breadboards: 1

parts:
  R1 = BBC MicroBit  # not connected
  SparkFun_micro_bit_Breakout1 = SparkFun micro:bit Breakout [part_number=BOB-13988]
  Squix1 = OLED 0.96" 128x64 I2C SSD1306
  DHT1 = DHT11 Humitidy and Temperature Sensor
  R2 = Resistor [tolerance=±5% resistance=220 package=THT]

nets:
  GND: SparkFun_micro_bit_Breakout1.GND, Squix1.GND, DHT1.GND
  3.3V: SparkFun_micro_bit_Breakout1.3.3V, Squix1.VCC, DHT1.VDD, R2.Pin_0
  N1: SparkFun_micro_bit_Breakout1.0, DHT1.DATA, R2.Pin_1
  N2: SparkFun_micro_bit_Breakout1.19, Squix1.SCL
  N3: SparkFun_micro_bit_Breakout1.20, Squix1.SCA

custom parts:
  BBC MicroBit: The BBC MICRO:BIT
  SparkFun micro:bit Breakout: The micro:bit breakout is a board that connects to the BBC micro:bit and expands the capabilities of the development platform by providing access to more pins and allowing for connections to the I2C and SPI buses. This breakout board for the micro:bit’s edge connector allows intermediate and advanced users to connect the micro:bit to breadboards and other sensors, motors, LEDs, and more! The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
  DHT11 Humitidy and Temperature Sensor: DHT11 Humidity and Temperature Sensor
